// Logisim project TestingCPUcardLogic.circ as structural Verilog: 2 circuits, main circuit DataDirLogic
module DataDirLogic (
  input  MREQb,
  input  IOSELb,
  input  RDb,
  input  M1b,
  input  BUSAKb
);

  wire and_1_out, and_2_out, nand_1_out, or_1_out;

  and and_1 (and_1_out, MREQb, IOSELb);
  nand nand_1 (nand_1_out, RDb, M1b, BUSAKb);
  or or_1 (or_1_out, and_1_out, RDb);
  and and_2 (and_2_out, or_1_out, nand_1_out);
  LED ReadBUS (.in(and_2_out));
  LED #(.active("false")) WriteBUS (.in(and_2_out));

  // Notes on the sheet:
  //   MREQb: initial=0x1
  //   IOSELb: initial=0x1
  //   RDb: initial=0x1
  //   M1b: initial=0x1
  //   BUSAKb: initial=0x1
endmodule

module BankRAM (
  input  A15,
  input  BA19,
  input  MREQ,
  output RAMCS2,
  output RAMCS1
);

  wire and_1_out, not_1_out, not_2_out;

  not not_1 (not_1_out, A15);
  not not_2 (not_2_out, BA19);
  or or_1 (RAMCS2, not_2_out, A15, MREQ);
  and and_1 (and_1_out, not_1_out, BA19);
  or or_2 (RAMCS1, and_1_out, MREQ);

  // Notes on the sheet:
  //   MREQ: initial=0x1
endmodule
