// Logisim project Glue_Logic.circ as structural Verilog: 2 circuits, main circuit main
module main (
  input  in_1,
  input  ROMDIS_B,
  input  RD_B,
  input  MREQ_B,
  output RAMSEL_B,
  output ROMSEL_B
);

  wire or_1_out, or_2_out;

  nand R (RAMSEL_B, in_1, ROMSEL_B);
  nand S (ROMSEL_B, RAMSEL_B, ROMDIS_B);
  or or_1 (or_1_out, RAMSEL_B, RD_B);
  or or_2 (or_2_out, ROMSEL_B, MREQ_B);
  LED #(.active("false")) ROMCS_B (.in(or_2_out));
  LED #(.active("false")) RAMOE_B (.in(or_1_out));

  // Notes on the sheet:
  //   in_1: pull=up
  //   ROMDIS_B: initial=0x1
  //   RD_B: initial=0x1
  //   MREQ_B: initial=0x1
endmodule

module RAMCS (
  input  MREQ,
  input  A15,
  input  BA22,
  input  BA21,
  input  BA20,
  input  BA19,
  output RAMCS1,
  output RAMCS2
);

  wire and_1_out, and_2_out, and_3_out, and_4_out, not_1_out, not_2_out;

  not not_1 (not_1_out, A15);
  not not_2 (not_2_out, BA19);
  and and_1 (and_1_out, not_1_out, BA19);
  and and_2 (and_2_out, not_1_out, BA20);
  and and_3 (and_3_out, not_1_out, BA21);
  and and_4 (and_4_out, not_1_out, BA22);
  or or_1 (RAMCS2, not_2_out, BA20, BA21, BA22, A15, MREQ);
  or or_2 (RAMCS1, and_1_out, and_2_out, and_3_out, and_4_out, MREQ);
endmodule
